// Logisim project CPU.circ as structural Verilog: 11 circuits, main circuit full_adder
module half_adder (
  input  A,
  input  B,
  output Co,
  output O
);

  and and_1 (Co, A, B);
  xor xor_1 (O, A, B);
endmodule

module full_adder (
  input  Ci,
  input  A,
  input  B,
  output Co,
  output O
);

  wire and_1_out, and_2_out, xor_1_out;

  and and_1 (and_1_out, A, B);
  and and_2 (and_2_out, Ci, xor_1_out);
  xor xor_1 (xor_1_out, A, B);
  or or_1 (Co, and_1_out, and_2_out);
  xor xor_2 (O, Ci, xor_1_out);
endmodule

module ripple_adder_8_bit (
  input  Ci,
  input  [7:0] A,
  input  [7:0] B,
  output [7:0] O,
  output Co
);

  wire full_adder_1_co, full_adder_2_co, full_adder_3_co, full_adder_4_co, full_adder_5_co, full_adder_6_co,
       full_adder_7_co;

  full_adder full_adder_1 (.Ci(Ci), .A(A[0]), .B(B[0]), .Co(full_adder_1_co), .O(O[0]));
  full_adder full_adder_2 (.Ci(full_adder_1_co), .A(A[1]), .B(B[1]), .Co(full_adder_2_co), .O(O[1]));
  full_adder full_adder_3 (.Ci(full_adder_2_co), .A(A[2]), .B(B[2]), .Co(full_adder_3_co), .O(O[2]));
  full_adder full_adder_4 (.Ci(full_adder_3_co), .A(A[3]), .B(B[3]), .Co(full_adder_4_co), .O(O[3]));
  full_adder full_adder_5 (.Ci(full_adder_4_co), .A(A[4]), .B(B[4]), .Co(full_adder_5_co), .O(O[4]));
  full_adder full_adder_6 (.Ci(full_adder_5_co), .A(A[5]), .B(B[5]), .Co(full_adder_6_co), .O(O[5]));
  full_adder full_adder_7 (.Ci(full_adder_6_co), .A(A[6]), .B(B[6]), .Co(full_adder_7_co), .O(O[6]));
  full_adder full_adder_8 (.Ci(full_adder_7_co), .A(A[7]), .B(B[7]), .Co(Co), .O(O[7]));
endmodule

module arithmetic_unit_8_bit (
  input  [7:0] A,
  input  [7:0] B,
  input  EO,
  input  SU,
  output [7:0] Q,
  output Co,
  output [7:0] ST
);

  wire [7:0] xor_8_out;

  xor xor_1 (xor_8_out[7], SU, B[7]);
  xor xor_2 (xor_8_out[6], SU, B[6]);
  xor xor_3 (xor_8_out[5], SU, B[5]);
  xor xor_4 (xor_8_out[4], SU, B[4]);
  xor xor_5 (xor_8_out[3], SU, B[3]);
  ripple_adder_8_bit ripple_adder_8_bit_1 (.Ci(SU), .A(A), .B(xor_8_out), .O(ST), .Co(Co));
  xor xor_6 (xor_8_out[2], SU, B[2]);
  assign Q = EO ? ST : 8'bz;  // Controlled_Buffer controlled_buffer_1
  xor xor_7 (xor_8_out[1], SU, B[1]);
  xor xor_8 (xor_8_out[0], SU, B[0]);
endmodule

module or_latch (
  input  S,
  output Q
);

  or or_1 (Q, S, Q);
endmodule

module sr_latch (
  input  R,
  input  S,
  output Q,
  output NQ
);

  nor nor_1 (Q, R, NQ);
  nor nor_2 (NQ, Q, S);
endmodule

module d_latch (
  input  D,
  input  E,
  output Q,
  output NQ
);

  wire and_1_out, and_2_out, not_1_out;

  not not_1 (not_1_out, D);
  and and_1 (and_1_out, not_1_out, E);
  and and_2 (and_2_out, E, D);
  sr_latch sr_latch_1 (.R(and_1_out), .S(and_2_out), .Q(Q), .NQ(NQ));
endmodule

module d_flip_flop (
  input  D,
  input  RCLK,
  output Q,
  output NQ
);

  D_Flip_Flop d_ff_1 (.D(D), .clk(RCLK), .Q(Q), .Qn(NQ));  // open: preset, reset
endmodule

module data_register (
  input  D,
  input  L,
  input  CLK,
  output Q
);

  wire and_1_out, and_2_out, not_1_out, or_1_out;

  not not_1 (not_1_out, L);
  and and_1 (and_1_out, Q, not_1_out);
  and and_2 (and_2_out, D, L);
  or or_1 (or_1_out, and_1_out, and_2_out);
  d_flip_flop d_flip_flop_1 (.D(or_1_out), .RCLK(CLK), .Q(Q));  // open: NQ
endmodule

module data_register_8_bit (
  input  [7:0] D,
  input  L,
  input  E,
  input  CLK,
  output [7:0] Q,
  output [7:0] ST
);

  data_register data_register_1 (.D(D[0]), .L(L), .CLK(CLK), .Q(ST[0]));
  data_register data_register_2 (.D(D[1]), .L(L), .CLK(CLK), .Q(ST[1]));
  data_register data_register_3 (.D(D[2]), .L(L), .CLK(CLK), .Q(ST[2]));
  data_register data_register_4 (.D(D[3]), .L(L), .CLK(CLK), .Q(ST[3]));
  data_register data_register_5 (.D(D[4]), .L(L), .CLK(CLK), .Q(ST[4]));
  data_register data_register_6 (.D(D[5]), .L(L), .CLK(CLK), .Q(ST[5]));
  data_register data_register_7 (.D(D[6]), .L(L), .CLK(CLK), .Q(ST[6]));
  data_register data_register_8 (.D(D[7]), .L(L), .CLK(CLK), .Q(ST[7]));
  assign Q = E ? ST : 8'bz;  // Controlled_Buffer controlled_buffer_1
endmodule

module main (
  input  PB,
  input  HLT,
  input  AL,
  input  AE,
  input  EO,
  input  SU,
  input  BL,
  input  BE,
  input  IL,
  input  IE
);

  wire and_1_out, CLK_out, not_1_out;
  wire [3:0] IR_st, IR_st_2;
  wire [7:0] A_st, ALU_st, B_st, controlled_buffer_1_out, dipswitch_1_sw8, IR_q;

  Clock CLK (.out(CLK_out));
  not not_1 (not_1_out, HLT);
  and and_1 (and_1_out, CLK_out, not_1_out);
  LedBar #(.matrixcols(4)) ledbar_1 (.led0(IR_st_2[3]), .led1(IR_st_2[2]), .led2(IR_st_2[1]), .led3(IR_st_2[0]));
  DipSwitch dipswitch_1 (
    .sw1(dipswitch_1_sw8[7]), .sw2(dipswitch_1_sw8[6]), .sw3(dipswitch_1_sw8[5]), .sw4(dipswitch_1_sw8[4]),
    .sw5(dipswitch_1_sw8[3]), .sw6(dipswitch_1_sw8[2]), .sw7(dipswitch_1_sw8[1]), .sw8(dipswitch_1_sw8[0]));
  LedBar #(.matrixcols(4)) ledbar_2 (.led0(IR_st[3]), .led1(IR_st[2]), .led2(IR_st[1]), .led3(IR_st[0]));
  data_register_8_bit IR (
    .D(controlled_buffer_1_out), .L(IL), .E(IE), .CLK(and_1_out), .Q(IR_q), .ST({IR_st_2, IR_st}));
  assign controlled_buffer_1_out = PB ? dipswitch_1_sw8 : 8'bz;  // Controlled_Buffer controlled_buffer_1
  assign controlled_buffer_1_out = IE ? {4'b0000, IR_q[3:0]} : 8'bz;  // Controlled_Buffer controlled_buffer_2
  LedBar ledbar_3 (
    .led0(controlled_buffer_1_out[7]), .led1(controlled_buffer_1_out[6]), .led2(controlled_buffer_1_out[5]),
    .led3(controlled_buffer_1_out[4]), .led4(controlled_buffer_1_out[3]), .led5(controlled_buffer_1_out[2]),
    .led6(controlled_buffer_1_out[1]), .led7(controlled_buffer_1_out[0]));
  LedBar ledbar_4 (
    .led0(A_st[7]), .led1(A_st[6]), .led2(A_st[5]), .led3(A_st[4]), .led4(A_st[3]), .led5(A_st[2]),
    .led6(A_st[1]), .led7(A_st[0]));
  LedBar ledbar_5 (
    .led0(ALU_st[7]), .led1(ALU_st[6]), .led2(ALU_st[5]), .led3(ALU_st[4]), .led4(ALU_st[3]),
    .led5(ALU_st[2]), .led6(ALU_st[1]), .led7(ALU_st[0]));
  LedBar ledbar_6 (
    .led0(B_st[7]), .led1(B_st[6]), .led2(B_st[5]), .led3(B_st[4]), .led4(B_st[3]), .led5(B_st[2]),
    .led6(B_st[1]), .led7(B_st[0]));
  data_register_8_bit A (
    .D(controlled_buffer_1_out), .L(AL), .E(AE), .CLK(and_1_out), .Q(controlled_buffer_1_out), .ST(A_st));
  arithmetic_unit_8_bit ALU (
    .A(A_st), .B(B_st), .EO(EO), .SU(SU), .Q(controlled_buffer_1_out), .ST(ALU_st));  // open: Co
  data_register_8_bit B (
    .D(controlled_buffer_1_out), .L(BL), .E(BE), .CLK(and_1_out), .Q(controlled_buffer_1_out), .ST(B_st));

  // Notes on the sheet:
  //   BUS
endmodule
